# Fritzing sketch mates (saved by Fritzing 0.8.7b)

parts:
  Součástka2 = Rotoshield - Motor driver shield for Arduino
  M1 = DC Motor
  M2 = DC Motor
  Součástka1 = Arduino Uno (Rev3)
  VCC1 = Battery
  Součástka3 = Bluetooth HC-05 Macho

nets:
  N1: Součástka2.DIG_0, Součástka1.D0/RX, Součástka3.TXD
  N2: Součástka2.DIG_1, Součástka1.D1/TX, Součástka3.RXD
  N3: Součástka2.DIG_2, Součástka1.D2
  N4: Součástka2.DIG_3, Součástka1.D3_PWM
  N5: Součástka2.DIG_4, Součástka1.D4
  N6: Součástka2.DIG_5, Součástka1.D5_PWM
  N7: Součástka2.DIG_6, Součástka1.D6_PWM
  N8: Součástka2.DIG_7, Součástka1.D7
  N9: Součástka2.A_IN_0, Součástka1.A0
  N10: Součástka2.A_IN_1, Součástka1.A1
  N11: Součástka2.A_IN_2, Součástka1.A2
  N12: Součástka2.A_IN_3, Součástka1.A3
  N13: Součástka2.A_IN_4, Součástka1.A4/SDA
  N14: Součástka2.A_IN_5, Součástka1.A5/SCL
  N15: Součástka2.DIG_8, Součástka1.D8
  N16: Součástka2.DIG_9, Součástka1.D9_PWM
  N17: Součástka2.DIG_10, Součástka1.D10_PWM/SS
  N18: Součástka2.DIG_11, Součástka1.D11_PWM/MOSI
  N19: Součástka2.DIG_12, Součástka1.D12/MISO
  N20: Součástka2.DIG_13, Součástka1.D13/SCK
  GND: Součástka2.GND, Součástka1.GND, VCC1.-, Součástka3.GND
  N21: Součástka2.AREF, Součástka1.AREF
  N22: Součástka2.VCC, VCC1.+
  N23: Součástka2.RESET, Součástka1.RESET
  +5V: Součástka2.+5V, Součástka1.5V, Součástka3.VCC
  VIN: Součástka2.VIN, Součástka1.VIN
  N24: Součástka2.M1-2, M1.pin_2
  N25: Součástka2.M1-1, M1.pin_1
  N26: Součástka2.M2-2, M2.pin_2
  N27: Součástka2.M2-1, M2.pin_1
